// Logisim project cpu.circ as structural Verilog: 1 circuit, main circuit cpu
module cpu (
  input  clk,
  input  [31:0] INSTRUCTION,
  input  [31:0] READ_DATA,
  output [31:0] WRITE_ADDRESS,
  output [31:0] PROGRAM_COUNTER,
  output [31:0] ra,
  output [31:0] sp,
  output [31:0] t0,
  output [31:0] t1,
  output [31:0] t2,
  output [31:0] s0,
  output [31:0] s1,
  output [31:0] a0,
  output [31:0] tohost,
  output [3:0] WRITE_ENABLE,
  output [31:0] WRITE_DATA
);

  wire ASel, BrEq, BrLt, BrUn, BSel, PCSel, RegWEn;
  wire [1:0] WBSel;
  wire [2:0] fun3, ImmSel;
  wire [3:0] ALUSel;
  wire [6:0] fun7;
  wire [24:0] Inst;
  wire [31:0] ALU_Result, data1, data2, imm, multiplexer_2_out, multiplexer_3_out, PC_add, WB;

  Multiplexer #(.enable("false"), .width(32)) multiplexer_1 (.in0(PC_add), .in1(ALU_Result), .sel(PCSel));  // open: out
  Adder #(.width(32)) adder_1 (.a(PROGRAM_COUNTER), .b(32'h4), .out(PC_add));  // open: cin, cout
  Register #(.width(32)) PC (.D(PC_add), .clk(clk), .Q(PROGRAM_COUNTER));  // open: en, clr
  Register #(.width(32)) register_1 (
    .D(INSTRUCTION), .clk(clk), .Q({fun7, Inst[24:15], fun3, Inst[11:0]}));  // open: en, clr
  control_logic control_logic_1 (
    .PCSel(PCSel), .RegWEn(RegWEn), .ImmSel(ImmSel), .BrUn(BrUn), .ASel(ASel), .BSel(BSel), .ALUSel(ALUSel),
    .WBSel(WBSel), .inst(INSTRUCTION), .BrEq(BrEq), .BrLt(BrLt));  // open: CSRWen, lb, lh, sb, sh, MemRW, CSRSel
  imm_gen imm_gen_1 (.inst({fun7, Inst[24:15], fun3, Inst[11:0]}), .ImmSel(3'b000), .imm(imm));
  regfile regfile_1 (
    .rs1(Inst[19:15]), .rs2(Inst[24:20]), .rd(Inst[11:7]), .Write_Data(WB), .RegWEn(1'b1), .clk(clk),
    .ra(ra), .sp(sp), .t0(t0), .t1(t1), .t2(t2), .s0(s0), .s1(s1), .a0(a0), .Read_Data_1(data1),
    .Read_Data_2(data2));
  branch_comp branch_comp_1 (.rs1(data1), .rs2(data2), .BrUn(BrUn), .BrEq(BrEq), .BrLt(BrLt));
  Multiplexer #(.enable("false"), .width(32)) multiplexer_2 (
    .in0(data1), .in1(PROGRAM_COUNTER), .out(multiplexer_2_out), .sel(1'b0));
  Multiplexer #(.enable("false"), .width(32)) multiplexer_3 (
    .in0(data2), .in1(imm), .out(multiplexer_3_out), .sel(1'b1));
  csr csr_1 (.tohost(tohost));  // open: CSR_address, CSR_din, CSR_WE, clk
  alu alu_1 (.Result(ALU_Result), .A(multiplexer_2_out), .B(multiplexer_3_out), .ALUSel(4'b0000));
  Multiplexer #(.enable("false"), .select(2), .width(32)) multiplexer_4 (
    .in1(ALU_Result), .in2(PC_add), .out(WB), .sel(2'b01));  // open: in0, in3

  // Other names for the same wires on the sheet: opcode[6:0] = Inst[6:0]; rd[4:0] = Inst[11:7];
  //   Inst (some bits) = {fun7, fun3}; rs1[4:0] = Inst[19:15]; rest[11:0] = {fun7, Inst[24:20]};
  //   rs2[4:0] = Inst[24:20]; immed[6:0] = fun7

  // Notes on the sheet:
  //   Output to IMEM
  //   IMEM (do **NOT** move this)
  //   Inputs from IMEM
  //   It is OK to move the PC, RegFile, ALU, MEM, Branch Comp, Imm Gen, and Control Logic to wherever is most convenient for you when constructing your CPU, and to delete this text
  //   Inputs/Outputs for testing. Do **NOT** move these.
  //   Outputs To DMEM
  //   DMEM (do **NOT** move this)
  //   Inputs From DMEM
endmodule
